// Logisim project Lab2.circ as structural Verilog: 4 circuits, main circuit main
module main (
  input  [7:0] a,
  input  [7:0] b,
  input  in_3,
  output out_4
);

  wire clock_1_out;
  wire [9:0] func_1_result;

  func func_1 (.start(in_3), .clk(clock_1_out), .a(a), .b(b), .result(func_1_result), .ready(out_4));
  Clock clock_1 (.out(clock_1_out));
  Register #(.width(10), .trigger("high")) register_1 (.D(func_1_result), .clk(1'b1));  // open: en, Q, clr
endmodule

module mult (
  input  [7:0] b,
  input  start,
  input  clk,
  input  [7:0] a,
  output ready,
  output [15:0] result
);

  wire and_2_out, bitselector_1_out, comparator_1_lt, inc, rst;
  wire [3:0] adder_1_out, ctr_q;
  wire [15:0] adder_2_out, bit_extender_1_out, shifter_1_out;

  Adder #(.width(4)) adder_1 (.a(4'b0001), .b(ctr_q), .out(adder_1_out));  // open: cin, cout
  not not_1 (rst, start);
  Counter #(.width(4), .max('h8)) ctr (
    .D(adder_1_out), .count(inc), .Q(ctr_q), .clk(clk), .clr(rst));  // open: load, carry
  Comparator #(.width(4), .mode("unsigned")) comparator_1 (
    .a(ctr_q), .b(4'b1000), .lt(comparator_1_lt));  // open: gt, eq
  and and_1 (inc, start, comparator_1_lt);
  BitSelector bitselector_1 (.in(b), .out(bitselector_1_out), .sel(ctr_q[2:0]));
  and and_2 (and_2_out, bitselector_1_out, inc);
  assign bit_extender_1_out = {{8{1'b0}}, a};  // Bit_Extender bit_extender_1
  Register #(.width(16)) register_1 (.D(adder_2_out), .en(and_2_out), .Q(result), .clk(clk), .clr(rst));
  Shifter #(.width(16)) shifter_1 (.in(bit_extender_1_out), .\dist (ctr_q), .out(shifter_1_out));
  not not_2 (ready, comparator_1_lt);
  Adder #(.width(16)) adder_2 (.a(result), .b(shifter_1_out), .out(adder_2_out));  // open: cin, cout

  // Notes on the sheet:
  //   start: pull=down
endmodule

module cbrt (
  input  clk,
  input  start,
  input  [7:0] sum,
  input  [7:0] a,
  output [7:0] smd1,
  output rd,
  output [7:0] smd2,
  output [2:0] out_8
);

  wire and_1_out, and_2_out, and_4_out, cmp, comparator_1_gt, comparator_2_eq, comparator_2_gt, counter_2_q,
       dec, inc, mul1, mul2, not_2_out, nrd_mul, or_1_out, or_2_out, or_3_out, or_4_out, or_5_out, or_6_out,
       or_7_out, rd_mul, rst, st_mul, start_t, sub, sync, upd, xor_1_out;
  wire [2:0] a_mul_q, multiplexer_3_out, multiplexer_5_out, res_sft, state;
  wire [3:0] multiplexer_1_out, s;
  wire [4:0] b_mul_q, bit_extender_1_out, multiplexer_2_out;
  wire [7:0] b, bit_extender_2_out, bit_extender_3_out, bit_extender_4_out, bit_extender_5_out,
       multiplexer_4_out, negator_1_out, negator_2_out, shifter_2_out, x;
  wire [15:0] mult_1_result, res_mul;

  not not_1 (rst, start);
  Multiplexer #(.width(4), .enable("false")) multiplexer_1 (
    .in0(sum[3:0]), .in1(4'b0110), .out(multiplexer_1_out), .sel(sync));
  or or_1 (or_1_out, sync, dec);
  Shifter #(.width(3)) shifter_1 (.in(out_8), .\dist (2'b01), .out(res_sft));
  not not_2 (not_2_out, comparator_1_gt);
  Register #(.width(4), .trigger("falling")) u_s (.D(multiplexer_1_out), .en(or_1_out), .Q(s), .clk(clk));  // open: clr
  or or_2 (or_2_out, start_t, upd, cmp, inc, sub, dec);
  Multiplexer #(.width(5), .enable("false")) multiplexer_2 (
    .in0(bit_extender_1_out), .in1(res_mul[4:0]), .out(multiplexer_2_out), .sel(upd));
  assign bit_extender_1_out = {{2{1'b0}}, res_sft};  // Bit_Extender bit_extender_1
  Counter #(.width(1), .max('h1), .ongoal("stay")) counter_1 (
    .count(not_2_out), .Q(rd), .clk(clk), .clr(rst));  // open: load, D, carry
  and and_1 (and_1_out, start, comparator_1_gt);
  Comparator #(.width(4)) comparator_1 (.a(s), .b(4'b1101), .gt(comparator_1_gt));  // open: eq, lt
  Decoder #(.select(3), .disabled(0)) decoder_1 (
    .out0(start_t), .out1(mul1), .out2(mul2), .out3(cmp), .out4(inc), .out5(sub), .out6(dec), .sel(state),
    .en(and_1_out));  // open: out7
  Counter #(.width(3), .max('h6), .trigger("falling")) u_state (
    .count(or_2_out), .Q(state), .clk(clk), .clr(rst));  // open: load, D, carry
  Counter #(.width(1), .max('h1), .ongoal("stay"), .trigger("falling")) counter_2 (
    .count(start), .Q(counter_2_q), .clk(clk), .clr(rst));  // open: load, D, carry
  Multiplexer #(.width(3), .enable("false")) multiplexer_3 (
    .in0(3'b011), .in1(sum[2:0]), .out(multiplexer_3_out), .sel(upd));
  or or_3 (or_3_out, start_t, upd);
  Multiplexer #(.width(8), .enable("false")) multiplexer_4 (
    .in0(a), .in1(sum), .out(multiplexer_4_out), .sel(counter_2_q));
  not not_3 (sync, counter_2_q);
  Register #(.trigger("falling")) u_x (.D(multiplexer_4_out), .en(xor_1_out), .Q(x), .clk(clk));  // open: clr
  xor xor_1 (xor_1_out, sync, and_2_out);
  Register #(.width(3), .trigger("falling")) a_mul (
    .D(multiplexer_3_out), .en(or_3_out), .Q(a_mul_q), .clk(clk), .clr(rst));
  assign bit_extender_2_out = {{5{1'b0}}, a_mul_q};  // Bit_Extender bit_extender_2
  assign bit_extender_3_out = {{3{1'b0}}, b_mul_q};  // Bit_Extender bit_extender_3
  Register #(.width(5), .trigger("falling")) b_mul (
    .D(multiplexer_2_out), .en(or_3_out), .Q(b_mul_q), .clk(clk), .clr(rst));
  Shifter shifter_2 (.in(sum), .\dist (s[2:0]), .out(shifter_2_out));
  Comparator #(.mode("unsigned")) comparator_2 (.a(x), .b(b), .gt(comparator_2_gt), .eq(comparator_2_eq));  // open: lt
  and and_2 (and_2_out, or_6_out, sub);
  mult mult_1 (
    .b(bit_extender_3_out), .start(st_mul), .a(bit_extender_2_out), .ready(rd_mul), .result(mult_1_result),
    .clk(clk));
  or or_4 (or_4_out, clk, nrd_mul);
  or or_5 (or_5_out, mul1, mul2);
  Register register_1 (.D(shifter_2_out), .en(cmp), .Q(b), .clk(clk), .clr(rst));
  or or_6 (or_6_out, comparator_2_gt, comparator_2_eq);
  and and_3 (st_mul, or_4_out, or_5_out);
  and and_4 (and_4_out, or_6_out, inc);
  not not_4 (nrd_mul, rd_mul);
  and and_5 (upd, rd_mul, clk);
  Register #(.width(16), .trigger("high")) result_mul (.D(mult_1_result), .Q(res_mul), .clk(st_mul));  // open: en, clr
  Multiplexer #(.width(3), .enable("false")) multiplexer_5 (
    .in0(res_sft), .in1(sum[2:0]), .out(multiplexer_5_out), .sel(and_4_out));
  or or_7 (or_7_out, start_t, and_4_out);
  Register #(.width(3), .trigger("falling")) result (
    .D(multiplexer_5_out), .en(or_7_out), .Q(out_8), .clk(clk), .clr(rst));
  assign bit_extender_4_out = {{5{1'b0}}, out_8};  // Bit_Extender bit_extender_4
  assign bit_extender_5_out = {{4{1'b0}}, s};  // Bit_Extender bit_extender_5
  Negator negator_1 (.in(b), .out(negator_1_out));
  Negator negator_2 (.in(8'h3), .out(negator_2_out));
  Multiplexer #(.select(3), .width(8), .disabled(0)) multiplexer_6 (
    .in2(bit_extender_4_out), .in3(res_mul[7:0]), .in4(bit_extender_4_out), .in5(x),
    .in6(bit_extender_5_out), .out(smd1), .sel(state), .en(start));  // open: in0, in1, in7
  Multiplexer #(.select(3), .width(8), .disabled(0)) multiplexer_7 (
    .in2(8'h1), .in3(8'h1), .in4(8'h1), .in5(negator_1_out), .in6(negator_2_out), .out(smd2), .sel(state),
    .en(start));  // open: in0, in1, in7

  // Other names for the same wires on the sheet: res[2:0] = out_8; st = start
endmodule

module func (
  input  start,
  input  clk,
  input  [7:0] a,
  input  [7:0] b,
  output [9:0] result,
  output ready
);

  wire act0, act1, and_1_out, and_2_out, and_4_out, and_5_out, and_6_out, counter_1_q, en_regs, nand_1_out,
       not_2_out, not_3_out, not_4_out, nrd_mul, or_1_out, or_3_out, rd_cbrt, rd_mul, ready_t, rst, save,
       start_t;
  wire [1:0] multer1_q, multiplexer_1_out, state_q;
  wire [2:0] cbrt_1_out_8;
  wire [7:0] bit_extender_4_out, cbrt_1_smd1, cbrt_1_smd2, demultiplexer_1_out0, multer2_q,
       multiplexer_3_out, res_cbrt;
  wire [9:0] adder_1_out, bit_extender_1_out, bit_extender_2_out, demultiplexer_1_out1, multiplexer_2_out,
       multiplexer_4_out, reg_mul, reg_mul2;
  wire [9:8] demultiplexer_1_out0_2;
  wire [15:0] mult_1_result;

  not not_1 (rst, start);
  or or_1 (or_1_out, and_1_out, and_2_out, start_t);
  and and_1 (and_1_out, rd_cbrt, rd_mul);
  and and_2 (and_2_out, rd_mul, act1);
  and and_3 (save, start, not_2_out);
  not not_2 (not_2_out, start_t);
  Decoder #(.select(2), .disabled(0)) decoder_1 (
    .out0(start_t), .out1(act0), .out2(act1), .out3(ready_t), .sel(state_q), .en(start));
  Counter #(.width(2), .max('h3), .ongoal("stay"), .trigger("falling")) state (
    .count(or_1_out), .Q(state_q), .clk(clk), .clr(rst));  // open: load, D, carry
  cbrt cbrt_1 (
    .start(save), .a(b), .rd(rd_cbrt), .out_8(cbrt_1_out_8), .smd1(cbrt_1_smd1), .sum(demultiplexer_1_out0),
    .smd2(cbrt_1_smd2), .clk(clk));
  Counter #(.width(1), .max('h1), .ongoal("stay"), .trigger("falling")) counter_1 (
    .count(start), .Q(counter_1_q), .clk(clk), .clr(rst));  // open: load, D, carry
  not not_3 (not_3_out, counter_1_q);
  Multiplexer #(.width(2), .enable("false")) multiplexer_1 (
    .in0(2'b11), .in1(2'b10), .out(multiplexer_1_out), .sel(counter_1_q));
  or or_2 (en_regs, not_3_out, rd_mul);
  assign bit_extender_1_out = {{2{1'b0}}, cbrt_1_smd1};  // Bit_Extender bit_extender_1
  Multiplexer #(.width(10), .enable("false")) multiplexer_2 (
    .in0(bit_extender_1_out), .in1(reg_mul), .out(multiplexer_2_out), .sel(ready_t));
  assign bit_extender_2_out = {{2{1'b0}}, cbrt_1_smd2};  // Bit_Extender bit_extender_2
  assign res_cbrt = {{5{1'b0}}, cbrt_1_out_8};  // Bit_Extender bit_extender_3
  Multiplexer #(.width(8), .enable("false")) multiplexer_3 (
    .in0(a), .in1(res_cbrt), .out(multiplexer_3_out), .sel(counter_1_q));
  Adder #(.width(10)) adder_1 (.a(multiplexer_2_out), .b(multiplexer_4_out), .out(adder_1_out));  // open: cin, cout
  Multiplexer #(.width(10), .enable("false")) multiplexer_4 (
    .in0(bit_extender_2_out), .in1(reg_mul2), .out(multiplexer_4_out), .sel(ready_t));
  Register #(.width(2), .trigger("falling")) multer1 (
    .D(multiplexer_1_out), .en(en_regs), .Q(multer1_q), .clk(clk), .clr(rst));
  Register #(.trigger("falling")) multer2 (.D(multiplexer_3_out), .en(en_regs), .Q(multer2_q), .clk(clk), .clr(rst));
  nand nand_1 (nand_1_out, rd_cbrt, rd_mul);
  Demultiplexer #(.width(10), .enable("false")) demultiplexer_1 (
    .out0({demultiplexer_1_out0_2, demultiplexer_1_out0}), .out1(demultiplexer_1_out1), .in(adder_1_out),
    .sel(ready_t));
  assign bit_extender_4_out = {{6{1'b0}}, multer1_q};  // Bit_Extender bit_extender_4
  mult mult_1 (
    .b(multer2_q), .start(and_4_out), .a(bit_extender_4_out), .ready(rd_mul), .result(mult_1_result),
    .clk(clk));
  and and_4 (and_4_out, or_3_out, save);
  or or_3 (or_3_out, nand_1_out, clk);
  not not_4 (not_4_out, rd_mul);
  Register #(.width(10), .trigger("high")) register_1 (
    .D(demultiplexer_1_out1), .Q(result), .clk(ready_t), .clr(rst));  // open: en
  not not_5 (nrd_mul, rd_mul);
  and and_5 (and_5_out, not_4_out, act0);
  Register #(.width(10), .trigger("falling")) u_reg_mul (
    .D(mult_1_result[9:0]), .Q(reg_mul), .clk(and_5_out), .clr(rst));  // open: en
  and and_6 (and_6_out, not_4_out, act1);
  Counter #(.width(1), .max('h1), .ongoal("stay")) counter_2 (
    .count(ready_t), .Q(ready), .clk(clk), .clr(rst));  // open: load, D, carry
  Register #(.width(10)) u_reg_mul2 (.D(mult_1_result[9:0]), .en(and_6_out), .Q(reg_mul2), .clk(clk), .clr(rst));

  // Other names for the same wires on the sheet: st = start
endmodule
