// Logisim project Lab4.circ as structural Verilog
module lfsr (
  input  clk,
  input  reset,
  input  [7:0] polynom,
  input  [7:0] init,
  output [7:0] lfsr_out,
  output ready
);

  wire and_3_out, bit_q, check, comparator_1_eq, comparator_1_lt, fdback, odd_parity_1_out, or_1_out,
       or_2_out, start, write;
  wire [1:0] state_q;
  wire [2:0] ctr_q;
  wire [7:0] and_1_out, bit_extender_1_out, multiplexer_1_out, sh_reg, shift, shifter_1_out;

  Multiplexer #(.width(8), .enable("false")) multiplexer_1 (
    .in0(shift), .in1(init), .out(multiplexer_1_out), .sel(reset));
  Register #(.trigger("falling")) shift_reg (.D(multiplexer_1_out), .en(or_1_out), .Q(sh_reg), .clk(clk));  // open: clr
  or or_1 (or_1_out, reset, write);
  Counter #(.width(3), .max('h7), .trigger("falling")) ctr (
    .count(check), .Q(ctr_q), .clk(clk), .clr(reset));  // open: load, D, carry
  assign and_1_out = sh_reg & polynom;  // AND_Gate and_1, 8 bits wide
  and and_2 (ready, comparator_1_eq, check);
  Comparator #(.width(3), .mode("unsigned")) comparator_1 (
    .a(ctr_q), .b(3'b111), .eq(comparator_1_eq), .lt(comparator_1_lt));  // open: gt
  and and_3 (and_3_out, check, comparator_1_lt);
  Shifter shifter_1 (.in(sh_reg), .\dist (3'b001), .out(shifter_1_out));
  Register #(.trigger("falling")) u_lfsr_out (.D(sh_reg), .en(ready), .Q(lfsr_out), .clk(clk));  // open: clr
  or or_2 (or_2_out, start, fdback, write, ready);
  xor odd_parity_1 (odd_parity_1_out, and_1_out[0], and_1_out[1], and_1_out[2], and_1_out[3], and_1_out[4], and_1_out[5], and_1_out[6], and_1_out[7]);
  Decoder #(.select(2), .enable("false")) decoder_1 (
    .out0(start), .out1(fdback), .out2(write), .out3(check), .sel(state_q));
  Counter #(.width(2), .max('h3), .trigger("falling")) state (
    .load(and_3_out), .D(2'b01), .count(or_2_out), .Q(state_q), .clk(clk), .clr(reset));  // open: carry
  Register #(.width(1), .trigger("falling")) \bit  (
    .D(odd_parity_1_out), .en(fdback), .Q(bit_q), .clk(clk));  // open: clr
  assign bit_extender_1_out = {{7{1'b0}}, bit_q};  // Bit_Extender bit_extender_1
  Adder adder_1 (.a(bit_extender_1_out), .b(shifter_1_out), .out(shift));  // open: cin, cout

  // Other names for the same wires on the sheet: poly[7:0] = polynom; rd = ready; rst = reset
endmodule

module crc8 (
  input  clk,
  input  reset,
  input  [9:0] data_in,
  input  start,
  input  [8:0] polynom,
  output ready,
  output [7:0] crc_out
);

  wire and_2_out, \bit , check, comparator_1_eq, comparator_1_lt, idle, multiplexer_2_out, not_1_out,
       or_1_out, or_2_out, shift, start_t, write, \xor ;
  wire [2:0] state_q;
  wire [3:0] counter_1_q;
  wire [7:0] crc, crc_q, multiplexer_1_out, shift_r;
  wire [9:0] bit_extender_1_out, data_q, xor_1_out;
  wire [10:0] bit_extender_2_out, bit_extender_3_out, multiplexer_3_out, shifter_1_out;
  wire [10:8] shift_reg_q, xor_2_out;

  Counter #(.width(4), .max('h9), .trigger("falling")) counter_1 (
    .count(check), .Q(counter_1_q), .clk(clk), .clr(reset));  // open: load, D, carry
  not not_1 (not_1_out, check);
  Comparator #(.width(4), .mode("unsigned")) comparator_1 (
    .a(counter_1_q), .b(4'b1001), .eq(comparator_1_eq), .lt(comparator_1_lt));  // open: gt
  Register #(.width(10), .trigger("falling")) data (.D(data_in), .en(start_t), .Q(data_q), .clk(clk));  // open: clr
  Multiplexer #(.width(8), .enable("false")) multiplexer_1 (
    .in0(shift_r), .in1(crc), .out(multiplexer_1_out), .sel(\bit ));
  or or_1 (or_1_out, not_1_out, comparator_1_eq);
  Multiplexer #(.enable("false")) multiplexer_2 (.in0(or_1_out), .in1(start), .out(multiplexer_2_out), .sel(idle));
  assign bit_extender_1_out = {{2{1'b0}}, crc_q};  // Bit_Extender bit_extender_1
  Register #(.trigger("falling")) u_crc (.D(multiplexer_1_out), .en(write), .Q(crc_q), .clk(clk), .clr(reset));
  and and_1 (ready, comparator_1_eq, check);
  and and_2 (and_2_out, check, comparator_1_lt);
  assign xor_1_out = data_q ^ bit_extender_1_out;  // XOR_Gate xor_1, 10 bits wide
  Register #(.trigger("falling")) register_1 (.D(crc_q), .en(ready), .Q(crc_out), .clk(clk));  // open: clr
  Decoder #(.select(3), .enable("false")) decoder_1 (
    .out0(idle), .out1(\xor ), .out2(shift), .out3(write), .out4(check), .sel(state_q));  // open: out5, out6, out7
  Counter #(.width(3), .max('h4), .trigger("falling")) state (
    .load(and_2_out), .D(3'b001), .count(multiplexer_2_out), .Q(state_q), .clk(clk), .clr(reset));  // open: carry
  assign bit_extender_2_out = {{1{1'b0}}, xor_1_out};  // Bit_Extender bit_extender_2
  and and_3 (start_t, idle, start);
  Register #(.width(11), .trigger("falling")) shift_reg (
    .D(multiplexer_3_out), .en(or_2_out), .Q({shift_reg_q, shift_r}), .clk(clk), .clr(reset));
  Multiplexer #(.width(11), .enable("false")) multiplexer_3 (
    .in0(bit_extender_2_out), .in1(shifter_1_out), .out(multiplexer_3_out), .sel(shift));
  or or_2 (or_2_out, \xor , shift);
  BitSelector #(.width(11)) bitselector_1 (.in({shift_reg_q, shift_r}), .out(\bit ), .sel(4'b1010));
  assign bit_extender_3_out = {{2{1'b0}}, polynom};  // Bit_Extender bit_extender_3
  Shifter #(.width(11)) shifter_1 (.in({shift_reg_q, shift_r}), .\dist (4'b0001), .out(shifter_1_out));
  assign {xor_2_out, crc} = {shift_reg_q, shift_r} ^ bit_extender_3_out;  // XOR_Gate xor_2, 11 bits wide

  // Other names for the same wires on the sheet: poly[8:0] = polynom; rd = ready; rst = reset; st = start
endmodule

module bist (
  input  test,
  input  clk,
  input  reset,
  input  in_4,
  output mux,
  output [7:0] lfsr1,
  output lfsr1_rd,
  output [7:0] lfsr2,
  output lfsr2_rd,
  output [7:0] test_mode_ctr
);

  Counter #(.width(1), .max('h1), .ongoal("stay")) counter_1 (
    .Q(mux), .clk(test), .clr(reset));  // open: load, D, count, carry
  lfsr lfsr_1 (.clk(clk), .reset(test), .polynom(8'ha9), .init(8'h64), .lfsr_out(lfsr1), .ready(lfsr1_rd));
  lfsr lfsr_2 (.clk(clk), .reset(test), .polynom(8'hd1), .init(8'h32), .lfsr_out(lfsr2), .ready(lfsr2_rd));
  Counter u_test_mode_ctr (.Q(test_mode_ctr), .clk(test), .clr(in_4));  // open: load, D, count, carry

  // Other names for the same wires on the sheet: rst = reset
endmodule
